# Fritzing sketch icestick_connection (saved by Fritzing 0.9.3b)
breadboards: 1

parts:
  Part1 = Adafruit MAX98357A I2S 3W Class D Amplifier [part_number="Adafruit #3006"]
  JP1 = Header 10 [package=1x10-2mm-smd]
  JP2 = Header 10 [package=1x10-2mm-smd]
  Part2 = Adafruit PDM Mic [part_number="Adafruit #3492"]

nets:
  N1: Part1.VIN, JP1.10
  N2: Part1.GND, JP1.9
  N3: Part1.DIN, JP1.6
  N4: Part1.BCLK, JP1.8
  N5: Part1.LRCLK, JP1.7
  N6: JP1.3, Part2.SELECT
  N7: JP1.4, Part2.DATA
  N8: JP1.5, Part2.CLK
  N9: JP2.9, Part2.GND
  N10: JP2.10, Part2.VDD

custom parts:
  Adafruit MAX98357A I2S 3W Class D Amplifier: Listen to this good news - we now have an all in one digital audio amp breakout board that works incredibly well with the Raspberry Pi! If you're looking for an easy and low cost way to get you digital sound files bumpin' then the MAX08357 I2S Amp Breakout is for you. It takes standard I2S digital audio input and, not only decodes it into analog, but also amplifies it directly into a speaker.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
  Adafruit PDM Mic: An exotic new microphone has arrived in the Adafruit shop, a PDM MEMS Microphone! PDM is the 'third' kind of microphone you can integrate with electronics, apart from analog or I2S. These microphones are very commonly used in products, but are rarely seen in maker projects. Still, they have some benefits so we thought we'd offer a breakout for the shop. The first thing to note is that this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
